# Fritzing sketch barsystem_breadboard (saved by Fritzing 0.8.5b)
breadboards: 2

parts:
  M1 = Stepper Motor - Bipolar
  Part1 = EasyDriver_v44
  M2 = DC Motor
  Q1 = npn-Powertransistor [package="TO220 [THT]"]
  Q2 = npn-Powertransistor [package="TO220 [THT]"]
  Q3 = npn-Powertransistor [package="TO220 [THT]"]
  Q4 = npn-Powertransistor [package="TO220 [THT]"]
  Q5 = npn-Powertransistor [package="TO220 [THT]"]
  Q6 = npn-Powertransistor [package="TO220 [THT]"]
  Q7 = npn-Powertransistor [package="TO220 [THT]"]
  Q8 = npn-Powertransistor [package="TO220 [THT]"]
  Q9 = npn-Powertransistor [package="TO220 [THT]"]
  Q10 = npn-Powertransistor [package="TO220 [THT]"]
  Q11 = npn-Powertransistor [package="TO220 [THT]"]
  D1 = Diode [package=diode-1n4001]
  RGB_SMD_LED1 = SMD RGB LED (WS2812) [package=5050]
  Part2 = Arduino Mega ADK (Rev3)
  Power_plug1 = Power plug
  Power_plug2 = Power plug
  M13 = DC Motor
  D2 = Diode [package=diode-1n4001]
  M14 = DC Motor
  D3 = Diode [package=diode-1n4001]
  M15 = DC Motor
  D4 = Diode [package=diode-1n4001]
  M16 = DC Motor
  D5 = Diode [package=diode-1n4001]
  M17 = DC Motor
  D6 = Diode [package=diode-1n4001]
  M18 = DC Motor
  D7 = Diode [package=diode-1n4001]
  M19 = DC Motor
  D8 = Diode [package=diode-1n4001]
  M20 = DC Motor
  D9 = Diode [package=diode-1n4001]
  M21 = DC Motor
  D10 = Diode [package=diode-1n4001]
  M22 = DC Motor
  D11 = Diode [package=diode-1n4001]
  R1 = Resistor [tolerance=±5% resistance=1k package=THT]
  R2 = Resistor [tolerance=±5% resistance=1k package=THT]
  R3 = Resistor [tolerance=±5% resistance=1k package=THT]
  R4 = Resistor [tolerance=±5% resistance=1k package=THT]
  R5 = Resistor [tolerance=±5% resistance=1k package=THT]
  R6 = Resistor [tolerance=±5% resistance=1k package=THT]
  R7 = Resistor [tolerance=±5% resistance=1k package=THT]
  R8 = Resistor [tolerance=±5% resistance=1k package=THT]
  R9 = Resistor [tolerance=±5% resistance=1k package=THT]
  R10 = Resistor [tolerance=±5% resistance=1k package=THT]
  R11 = Resistor [tolerance=±5% resistance=1k package=THT]
  L1 = Solenoid
  L2 = Solenoid
  D12 = Diode [package=diode-1n4001]
  D13 = Diode [package=diode-1n4001]
  Q12 = npn-Powertransistor [package="TO220 [THT]"]
  Q13 = npn-Powertransistor [package="TO220 [THT]"]
  R12 = Resistor [tolerance=±5% resistance=2.2k package=THT]
  R13 = Resistor [tolerance=±5% resistance=2.2k package=THT]
  C1 = Electrolytic Capacitor [capacitance=1mF package="200 mil [THT, electrolytic]"]

nets:
  N1: M1.A, Part1.OUT2A
  N2: M1.C, Part1.OUT2B
  N3: M1.B, Part1.OUT1A
  N4: M1.D, Part1.OUT1B
  GND: Part1.GND, Q1.emitter, Q2.emitter, Q3.emitter, Q4.emitter, Q5.emitter, Q6.emitter, Q7.emitter, Q8.emitter, Q9.emitter, Q10.emitter, Q11.emitter, RGB_SMD_LED1.VSS, Part2.GND, Power_plug1.GND, Power_plug2.GND, Q12.emitter, Q13.emitter, C1.-
  VIN: Part1.V+, Part2.VIN, Power_plug1.VCC, L1.pin2, L2.pin2, D12.A, D13.A
  N5: Part1.STEP, Part2.D35
  N6: Part1.DIR, Part2.D34
  VDD: M2.pin_1, D1.A, RGB_SMD_LED1.VDD, Power_plug2.VCC, M13.pin_1, D2.A, M14.pin_1, D3.A, M15.pin_1, D4.A, M16.pin_1, D5.A, M17.pin_1, D6.A, M18.pin_1, D7.A, M19.pin_1, D8.A, M20.pin_1, D9.A, M21.pin_1, D10.A, M22.pin_1, D11.A, C1.+
  N7: M2.pin_2, Q9.collector, D1.C
  N8: Q1.base, R6.Pin_0
  N9: Q1.collector, M15.pin_2, D4.C
  N10: Q2.base, R7.Pin_0
  N11: Q2.collector, M16.pin_2, D5.C
  N12: Q3.base, R8.Pin_0
  N13: Q3.collector, M17.pin_2, D6.C
  N14: Q4.base, R9.Pin_0
  N15: Q4.collector, M18.pin_2, D7.C
  N16: Q5.base, R10.Pin_0
  N17: Q5.collector, M19.pin_2, D8.C
  N18: Q6.base, R11.Pin_0
  N19: Q6.collector, M21.pin_2, D10.C
  N20: Q7.base, R5.Pin_0
  N21: Q7.collector, M14.pin_2, D3.C
  N22: Q8.base, R4.Pin_0
  N23: Q8.collector, M13.pin_2, D2.C
  N24: Q9.base, R3.Pin_0
  N25: Q10.base, R2.Pin_0
  N26: Q10.collector, M20.pin_2, D9.C
  N27: Q11.base, R1.Pin_0
  N28: Q11.collector, M22.pin_2, D11.C
  N29: RGB_SMD_LED1.DIn, Part2.D36
  N30: Part2.D22, R1.Pin_1
  N31: Part2.D23, Part2.D24, R2.Pin_1
  N32: Part2.D25, R4.Pin_1
  N33: Part2.D26, R5.Pin_1
  N34: Part2.D27, R6.Pin_1
  N35: Part2.D28, R7.Pin_1
  N36: Part2.D29, R8.Pin_1
  N37: Part2.D31, R10.Pin_1
  N38: Part2.D32, R11.Pin_1
  N39: Part2.D38, R13.Pin_0
  N40: Part2.D39, R12.Pin_0
  N41: L1.pin1, D13.C, Q12.collector
  N42: L2.pin1, Q13.collector
  N43: Q12.base, R12.Pin_1
  N44: Q13.base, R13.Pin_1

notes:
  12V
  5V
