# Fritzing sketch pcb-design (saved by Fritzing 0.9.0b)
circuit board: 16.7521cm x 8.37606cm
breadboards: 1

parts:
  DIGITAL_IO = female pin header, 8 pins [form="♀ (female)"]
  DIGITAL_IO_2 = female pin header, 10 pins [form="♀ (female)"]  # not connected
  Q1 = npn-Powertransistor [package="TO220 [THT]"]
  Q2 = npn-Powertransistor [package="TO220 [THT]"]
  Q3 = npn-Powertransistor [package="TO220 [THT]"]
  Q4 = npn-Powertransistor [package="TO220 [THT]"]
  Q5 = npn-Powertransistor [package="TO220 [THT]"]
  Q6 = npn-Powertransistor [package="TO220 [THT]"]
  Q7 = npn-Powertransistor [package="TO220 [THT]"]
  Q8 = npn-Powertransistor [package="TO220 [THT]"]
  Q9 = npn-Powertransistor [package="TO220 [THT]"]
  Q10 = npn-Powertransistor [package="TO220 [THT]"]
  Q11 = npn-Powertransistor [package="TO220 [THT]"]
  Q12 = npn-Powertransistor [package="TO220 [THT]"]
  CAP_1000uF = Electrolytic Capacitor [capacitance=1000µF package="300 mil [THT, electrolytic]"]
  Q13 = npn-Powertransistor [package="TO220 [THT]"]
  R1 = Resistor [tolerance=±5% resistance=1k package=THT]
  R2 = Resistor [tolerance=±5% resistance=1k package=THT]
  R3 = Resistor [tolerance=±5% resistance=1k package=THT]
  R4 = Resistor [tolerance=±5% resistance=1k package=THT]
  R5 = Resistor [tolerance=±5% resistance=1k package=THT]
  R6 = Resistor [tolerance=±5% resistance=1k package=THT]
  R7 = Resistor [tolerance=±5% resistance=1k package=THT]
  R8 = Resistor [tolerance=±5% resistance=1k package=THT]
  R9 = Resistor [tolerance=±5% resistance=1k package=THT]
  R10 = Resistor [tolerance=±5% resistance=1k package=THT]
  R11 = Resistor [tolerance=±5% resistance=1k package=THT]
  R12 = Resistor [tolerance=±5% resistance=2.2k package=THT]
  R13 = Resistor [tolerance=±5% resistance=2.2k package=THT]
  VIN = female pin header, 1 pin [form="♀ (female)"]
  RST_3_3V_5V = female pin header, 5 pins [form="♀ (female)"]
  DIGITAL_TX/RX = female pin header, 8 pins [form="♀ (female)"]
  LED = female pin header, 3 pins [form="♀ (female)"]
  ANALOG_IO = female pin header, 7 pins [form="♀ (female)"]  # not connected
  MOTORS = female pin header, 5 pins [form="♀ (female)"]
  GND = female pin header, 1 pin [form="♀ (female)"]
  VLV_GND = female pin header, 2 pins [form="♀ (female)"]
  GND_2 = female pin header, 1 pin [form="♀ (female)"]
  ANALOG_IO_2 = female pin header, 7 pins [form="♀ (female)"]  # not connected
  GND_3 = female pin header, 2 pins [form="♀ (female)"]
  5V_IN = Power plug
  DIGITAL_IO_PINS = double row female pin header, 30 pins [form="♀ (female)"]
  EASYDRIVER = EasyDriver_v44
  12V_IN = Power plug
  STEPPER = female pin header, 4 pins [form="♀ (female)"]
  GND_4 = female pin header, 2 pins [form="♀ (female)"]
  VLV_12V = female pin header, 2 pins [form="♀ (female)"]
  MOTORS_2 = female pin header, 3 pins [form="♀ (female)"]
  RX/VCC = female pin header, 2 pins [form="♀ (female)"]
  ESP8266 = female pin header, 2 pins [form="♀ (female)"]
  GND/TX = female pin header, 1 pin [form="♀ (female)"]
  R_2K = Resistor [tolerance=±5% resistance=2k package=THT]
  R_1K = Resistor [tolerance=±5% resistance=220 package=THT]
  R_3_3K = Resistor [tolerance=±5% resistance=3.3k package=THT]
  5V = female pin header, 2 pins [form="♀ (female)"]

nets:
  N1: DIGITAL_IO.pin5, EASYDRIVER.STEP
  N2: DIGITAL_IO.pin6, EASYDRIVER.DIR
  N3: Q1.base, R1.Pin_1
  N4: Q1.collector, MOTORS.pin1
  GND: Q1.emitter, Q2.emitter, Q3.emitter, Q4.emitter, Q5.emitter, Q6.emitter, Q7.emitter, Q8.emitter, Q9.emitter, Q10.emitter, Q11.emitter, Q12.emitter, CAP_1000uF.-, Q13.emitter, LED.pin3, GND_2.pin1, GND_3.pin1, GND_3.pin2, 5V_IN.GND, EASYDRIVER.GND, 12V_IN.GND, ESP8266.pin2, R_2K.Pin_0
  N5: Q2.base, R2.Pin_0
  N6: Q2.collector, MOTORS.pin2
  N7: Q3.base, R3.Pin_0
  N8: Q3.collector, MOTORS.pin3
  N9: Q4.base, R4.Pin_0
  N10: Q4.collector, MOTORS.pin4
  N11: Q5.base, R5.Pin_0
  N12: Q5.collector, MOTORS.pin5
  N13: Q6.base, R6.Pin_0
  N14: Q6.collector, GND.pin1
  N15: Q7.base, R7.Pin_0
  N16: Q7.collector, GND_4.pin1
  N17: Q8.base, R8.Pin_0
  N18: Q8.collector, GND_4.pin2
  N19: Q9.base, R9.Pin_0
  N20: Q9.collector, MOTORS_2.pin1
  N21: Q10.base, R10.Pin_0
  N22: Q10.collector, MOTORS_2.pin2
  N23: Q11.base, R11.Pin_0
  N24: Q11.collector, MOTORS_2.pin3
  N25: Q12.base, R12.Pin_0
  N26: Q12.collector, VLV_GND.pin1
  N27: CAP_1000uF.+, LED.pin1, 5V_IN.VCC, 5V.pin1, 5V.pin2
  N28: Q13.base, R13.Pin_0
  N29: Q13.collector, VLV_GND.pin2
  N30: R1.Pin_0, DIGITAL_IO_PINS.pin2
  N31: R2.Pin_1, DIGITAL_IO_PINS.pin3
  N32: R3.Pin_1, DIGITAL_IO_PINS.pin4
  N33: R4.Pin_1, DIGITAL_IO_PINS.pin5
  N34: R5.Pin_1, DIGITAL_IO_PINS.pin6
  N35: R6.Pin_1, DIGITAL_IO_PINS.pin7
  N36: R7.Pin_1, DIGITAL_IO_PINS.pin8
  N37: R8.Pin_1, DIGITAL_IO_PINS.pin9
  N38: R9.Pin_1, DIGITAL_IO_PINS.pin10
  N39: R10.Pin_1, DIGITAL_IO_PINS.pin11
  N40: R11.Pin_1, DIGITAL_IO_PINS.pin12
  N41: R12.Pin_1, DIGITAL_IO_PINS.pin13
  N42: R13.Pin_1, DIGITAL_IO_PINS.pin14
  N43: VIN.pin1, EASYDRIVER.V+, 12V_IN.VCC, VLV_12V.pin1, VLV_12V.pin2
  N44: RST_3_3V_5V.pin4, RX/VCC.pin1, R_3_3K.Pin_0
  N45: DIGITAL_TX/RX.pin5, R_1K.Pin_1
  N46: DIGITAL_TX/RX.pin6, ESP8266.pin1
  N47: LED.pin2, DIGITAL_IO_PINS.pin15
  N48: DIGITAL_IO_PINS.pin1, DIGITAL_IO_PINS.pin30
  N49: EASYDRIVER.OUT2A, STEPPER.pin1
  N50: EASYDRIVER.OUT2B, STEPPER.pin2
  N51: EASYDRIVER.OUT1A, STEPPER.pin3
  N52: EASYDRIVER.OUT1B, STEPPER.pin4
  N53: RX/VCC.pin2, R_2K.Pin_1, R_1K.Pin_0
  N54: GND/TX.pin1, R_3_3K.Pin_1
